# Fritzing sketch accident (saved by Fritzing 0.9.3b)
breadboards: 1

parts:
  Part1 = Arduino Mega 2560 (Rev3)
  GSM_SIM_GPSR_SMS_SIM900_SIM1 = SIM800L [package=THT]
  Shock_Sensor = LM393 vibration sensor breakout [part_number=100031]
  U1 = SUP500F [package=sup500f]

nets:
  GND: Part1.GND, GSM_SIM_GPSR_SMS_SIM900_SIM1.GND, Shock_Sensor.GND, U1.GND
  N1: Part1.D13_PWM, GSM_SIM_GPSR_SMS_SIM900_SIM1.SIM_RXD
  N2: Part1.D12_PWM, GSM_SIM_GPSR_SMS_SIM900_SIM1.SIM_TXD
  N3: Part1.D11_PWM, U1.RX-I
  N4: Part1.D10_PWM, U1.TX-O
  5V: Part1.VIN
  N5: Part1.D7_PWM, Shock_Sensor.DO
  VCC: GSM_SIM_GPSR_SMS_SIM900_SIM1.5V, Shock_Sensor.VCC, U1.VCC
