# Fritzing sketch alcohol (saved by Fritzing 0.9.3b)
breadboards: 1

parts:
  WeMos_D1_Mini1 = WeMos D1 Mini
  Buzzer = Piezo Speaker
  LED_Status = RGB LED (com. cathode, rbg) [package="5 mm [THT]"]
  Push_Button = Round Pushbutton
  Alcohol_Sensor = GAS_SENSOR [package=mq-3]
  LCD2 = LCD screen
  LCM1602_IIC2 = LCM1602 IIC [part_number="LCM1602 IIC" chip_label="LCM1602 IIC" package="DIP (Dual Inline) [THT]"]
  R1 = Resistor [tolerance=±5% resistance=220 package="2010 [SMD]"]
  R2 = Resistor [tolerance=±5% resistance=220 package="2010 [SMD]"]
  R3 = Resistor [tolerance=±5% resistance=220 package="2010 [SMD]"]
  R4 = Resistor [tolerance=±5% resistance=220 package="2010 [SMD]"]

nets:
  5V: WeMos_D1_Mini1.5V, Push_Button.leg0, Alcohol_Sensor.H2, LCM1602_IIC2.VCC
  N1: WeMos_D1_Mini1.A0, Alcohol_Sensor.A1
  N2: WeMos_D1_Mini1.D1, LCM1602_IIC2.SCL
  N3: WeMos_D1_Mini1.D2, LCM1602_IIC2.SDA
  N4: WeMos_D1_Mini1.D3, R1.Pin_1
  N5: WeMos_D1_Mini1.D4, R2.Pin_1
  N6: WeMos_D1_Mini1.D5, R3.Pin_1
  N7: WeMos_D1_Mini1.D6, Push_Button.leg1, R4.Pin_0
  N8: WeMos_D1_Mini1.D7, Buzzer.pin2
  N9: WeMos_D1_Mini1.G, Buzzer.pin1, LED_Status.common_cathode, Alcohol_Sensor.H1, LCM1602_IIC2.GND, R4.Pin_1
  N10: LED_Status.red_anode, R1.Pin_0
  N11: LED_Status.blue_anode, R2.Pin_0
  N12: LED_Status.green_anode, R3.Pin_0
  VSS: LCD2.VSS, LCM1602_IIC2.VSS
  VDD: LCD2.VDD, LCM1602_IIC2.VDD
  N13: LCD2.V0, LCM1602_IIC2.V0
  N14: LCD2.RS, LCM1602_IIC2.RS
  N15: LCD2.R/W, LCM1602_IIC2.RW
  N16: LCD2.E, LCM1602_IIC2.E
  N17: LCD2.DB0, LCM1602_IIC2.D0
  N18: LCD2.DB1, LCM1602_IIC2.D1
  N19: LCD2.DB2, LCM1602_IIC2.D2
  N20: LCD2.DB3, LCM1602_IIC2.D3
  N21: LCD2.DB4, LCM1602_IIC2.D4
  N22: LCD2.DB5, LCM1602_IIC2.D5
  N23: LCD2.DB6, LCM1602_IIC2.D6
  N24: LCD2.DB7, LCM1602_IIC2.D7
  N25: LCD2.LED+, LCM1602_IIC2.A
  N26: LCD2.LED-, LCM1602_IIC2.K
  N27: LCM1602_IIC2.LED_A, LCM1602_IIC2.LED_B

custom parts:
  LCM1602 IIC: I2C-Module to use a 1602 or 2004 LCD on with the wire.h libory Serial LCD Modul
