# Fritzing sketch drainage (saved by Fritzing 0.9.3b)
breadboards: 1

parts:
  Arduino_MEGA = Arduino Mega ADK (Rev3)
  DHT22 = Humidity and Temperature Sensor RHT03
  Ultrasonic_Sensor = HC-SR04 Ultrasonic Distance Sensor
  SIM800L = SIM800L [package=THT]
  Flow_Meter = YF-S201 Water Flow Meter

nets:
  GND: Arduino_MEGA.GND, DHT22.GND_2, Ultrasonic_Sensor.ECHO, SIM800L.GND, Flow_Meter.GND
  N1: Arduino_MEGA.D10_PWM, Ultrasonic_Sensor.GND
  N2: Arduino_MEGA.D9_PWM, Ultrasonic_Sensor.TRIG
  N3: Arduino_MEGA.D8_PWM, DHT22.Data-signal
  5V: Arduino_MEGA.IOREF, Arduino_MEGA.5V, DHT22.Vcc, Ultrasonic_Sensor.VCC, SIM800L.5V, Flow_Meter.VCC
  N4: Arduino_MEGA.D0/RX0, SIM800L.SIM_TXD
  N5: Arduino_MEGA.D1/TX0, SIM800L.SIM_RXD
  N6: Arduino_MEGA.D2_PWM, Flow_Meter.SIG

custom parts:
  YF-S201 Water Flow Meter: The YF-S201 Flow Meter. The input voltage is 5V to 24V (DC).
