# Fritzing sketch gatepass_schematic (saved by Fritzing 0.9.3b)
breadboards: 1

parts:
  Raspberry_Pi_1 = Raspberry Pi 3 [part_number=RPI-3-V1.2]
  Arduino_Nano = Arduino Nano (Rev3.0)
  Ultrasonic_Sensor_1 = HC-SR04 Ultrasonic Distance Sensor
  Ultrasonic_Sensor_2 = HC-SR04 Ultrasonic Distance Sensor
  J1 = Basic Servo
  Switch = SWITCH-MOMENTARY-2 [package=tactile-switch-1101ne]

nets:
  GND: Raspberry_Pi_1.GND, Arduino_Nano.GND
  N1: Raspberry_Pi_1.GPIO15, Arduino_Nano.D1/TX
  N2: Raspberry_Pi_1.GPIO14, Arduino_Nano.D0/RX
  5V: Raspberry_Pi_1.5V, Arduino_Nano.5V, Ultrasonic_Sensor_1.VCC, Ultrasonic_Sensor_2.VCC, J1.vcc, Switch.2
  N3: Arduino_Nano.D2, Ultrasonic_Sensor_1.TRIG
  N4: Arduino_Nano.D3, Ultrasonic_Sensor_1.GND
  N5: Arduino_Nano.D6, Ultrasonic_Sensor_2.TRIG
  N6: Arduino_Nano.D7, Ultrasonic_Sensor_2.GND
  N7: Arduino_Nano.D9, J1.pulse
  N8: Arduino_Nano.D10, Switch.1
  N9: Ultrasonic_Sensor_1.ECHO, Ultrasonic_Sensor_2.ECHO, J1.gnd
