# Fritzing sketch sensor (saved by Fritzing 0.9.3b)

parts:
  WeMos_D1_Mini1 = WeMos D1 Mini
  DHT22 = Humidity and Temperature Sensor RHT03
  CO2_Sensor = MLX90614 [package=to-39]

nets:
  5V: WeMos_D1_Mini1.5V, DHT22.Vcc, CO2_Sensor.VSS
  N1: WeMos_D1_Mini1.D1, CO2_Sensor.SCL_VZ
  N2: WeMos_D1_Mini1.D2, CO2_Sensor.PWM_SDA
  N3: WeMos_D1_Mini1.D5, DHT22.Data-signal
  N4: WeMos_D1_Mini1.G, DHT22.GND_2, CO2_Sensor.VDD
