# Fritzing sketch insulin_schem (saved by Fritzing 0.9.3b)
breadboards: 1

parts:
  WeMos_D1_Mini1 = WeMos D1 Mini
  GSM_SIM_GPSR_SMS_SIM900_SIM1 = SIM800L [package=THT]
  DHT22 = Humidity and Temperature Sensor RHT03
  Buzzer = Buzzer 12mm [package=buzzer-ccv]

nets:
  5V: WeMos_D1_Mini1.5V, DHT22.Vcc
  N1: WeMos_D1_Mini1.D1, DHT22.Data-signal
  N2: WeMos_D1_Mini1.D5, Buzzer.2
  N3: WeMos_D1_Mini1.D7, GSM_SIM_GPSR_SMS_SIM900_SIM1.SIM_TXD
  N4: WeMos_D1_Mini1.D8, GSM_SIM_GPSR_SMS_SIM900_SIM1.SIM_RXD
  GND: WeMos_D1_Mini1.G, GSM_SIM_GPSR_SMS_SIM900_SIM1.GND, DHT22.GND_2, Buzzer.1
  5V_2: GSM_SIM_GPSR_SMS_SIM900_SIM1.5V
