# Fritzing sketch wallettracking_schematic (saved by Fritzing 0.9.3b)
breadboards: 1

parts:
  Bluetooth = Bluetooth HC-05 Macho
  Buzzer = Piezo Speaker
  GPS/GPRS = LightBlue Bean
  Battery = 4 x AAA Battery Mount

nets:
  5V: Bluetooth.VCC, Buzzer.pin1, GPS/GPRS.VCC
  N1: Bluetooth.Key, Buzzer.pin2
  GND: Bluetooth.GND, GPS/GPRS.GND, Battery.-
  N2: GPS/GPRS.BAT, Battery.+
